# Fritzing sketch Pinnochio (saved by Fritzing 0.7.10b)
perfboards: 1

parts:
  IC1 = H-Bridge [package=THT]
  VCC1 = Battery block 9V
  Arduino1 = Arduino
  R1 = Slide Potentiometer
  M2 = DC Motor
  R2 = Slide Potentiometer
  M1 = DC Motor

nets:
  N1: IC1.1_2EN, Arduino1.D11
  N2: IC1.1A, Arduino1.D10
  N3: IC1.1Y, M2.pin_2
  GND1: IC1.GND1, IC1.GND2, IC1.GND3, IC1.GND4, VCC1.-, R2.wiper
  N4: IC1.2Y, M2.pin_1
  N5: IC1.2A, Arduino1.D9
  N6: IC1.VCC2, VCC1.+
  N7: IC1.3_4EN, Arduino1.D3
  N8: IC1.3A, IC1.4A, Arduino1.D6, Arduino1.D5
  N9: IC1.3Y, M1.pin_2
  N10: IC1.4Y, M1.pin_1
  N11: IC1.VCC1, Arduino1.+5V, R1.leg1
  N12: Arduino1.A3, R1.leg2
  N13: Arduino1.A5, R2.leg2
